# Fritzing sketch WiringSketch (saved by Fritzing 1.0.4)

parts:
  M1 = ESP32-S3-DevKitC-1-N8R8-v1 [part_number=ESP32-S3-DevKitC-1-N8R8-v1]
  A1 = 4in spi lcd display
  Capacitive_Soil_Moisture_Sensor1 = DFRobot Capacitive Soil Moisture Sensor V1.0 [part_number=SEN0193]
  Capacitive_Soil_Moisture_Sensor2 = DFRobot Capacitive Soil Moisture Sensor V1.0 [part_number=SEN0193]
  Capacitive_Soil_Moisture_Sensor3 = DFRobot Capacitive Soil Moisture Sensor V1.0 [part_number=SEN0193]
  Capacitive_Soil_Moisture_Sensor4 = DFRobot Capacitive Soil Moisture Sensor V1.0 [part_number=SEN0193]
  Capacitive_Soil_Moisture_Sensor5 = DFRobot Capacitive Soil Moisture Sensor V1.0 [part_number=SEN0193]
  Capacitive_Soil_Moisture_Sensor6 = DFRobot Capacitive Soil Moisture Sensor V1.0 [part_number=SEN0193]
  Capacitive_Soil_Moisture_Sensor7 = DFRobot Capacitive Soil Moisture Sensor V1.0 [part_number=SEN0193]
  Capacitive_Soil_Moisture_Sensor8 = DFRobot Capacitive Soil Moisture Sensor V1.0 [part_number=SEN0193]

nets:
  N1: M1.pin_1, M1.pin_2, A1.Pin_1, Capacitive_Soil_Moisture_Sensor1.VCC
  N2: M1.pin_4, Capacitive_Soil_Moisture_Sensor1.A
  N3: M1.pin_5, Capacitive_Soil_Moisture_Sensor2.A
  N4: M1.pin_6, Capacitive_Soil_Moisture_Sensor3.A
  N5: M1.pin_7, Capacitive_Soil_Moisture_Sensor4.A
  N6: M1.pin_8, Capacitive_Soil_Moisture_Sensor6.A
  N7: M1.pin_9, Capacitive_Soil_Moisture_Sensor8.A
  N8: M1.pin_10, Capacitive_Soil_Moisture_Sensor7.A
  N9: M1.pin_11, Capacitive_Soil_Moisture_Sensor5.A
  N10: M1.pin_15, A1.Pin_14
  N11: M1.pin_16, A1.Pin_11
  N12: M1.pin_17, A1.Pin_12
  N13: M1.pin_18, A1.Pin_10
  N14: M1.pin_19, A1.Pin_13
  N15: M1.pin_22, M1.pin_44, A1.Pin_2, Capacitive_Soil_Moisture_Sensor1.GND
  N16: M1.pin_36, A1.Pin_6
  N17: M1.pin_37, A1.Pin_7
  N18: M1.pin_38, A1.Pin_9
  N19: M1.pin_39, A1.Pin_3
  N20: M1.pin_40, A1.Pin_4
  N21: M1.pin_41, A1.Pin_5

custom parts:
  ESP32-S3-DevKitC-1-N8R8-v1: ESP32-S3-DevKitC-1-N8R8-v1 This module is 44pins long (2x22) and 11 pins width.
  4in spi lcd display: 4.0inch color screen with 320x480 resolution of 65K colors and rich display colors.
  DFRobot Capacitive Soil Moisture Sensor V1.0: DFRobot Capacitive Soil Moisture Sensor V1.0 This product measures soil moisture levels by capacitive sensing, rather than resistive sensing like other types of moisture sensor. It is made of a corrosion resistant material giving it a long service life. Insert it into soil and impress your friends with the real-time soil moisture data! The product includes an on-board voltage regulator which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
